# Fritzing sketch AES_PCB (saved by Fritzing 0.9.4)
breadboards: 1

parts:
  Part1 = Arduino Mega 2560 (Rev3)
  S1 = Pushbutton [package="[THT]"]
  S2 = Pushbutton [package="[THT]"]
  S3 = Pushbutton [package="[THT]"]
  S4 = Pushbutton [package="[THT]"]
  R1 = Resistor [tolerance=±5% resistance=10k package=THT]
  R4 = Resistor [tolerance=±5% resistance=10k package=THT]
  R5 = Resistor [tolerance=±5% resistance=10k package=THT]
  R6 = Resistor [tolerance=±5% resistance=10k package=THT]
  Part2 = Thumb Joystick
  DFRobot_DFPlayer_Mini1 = DFRobot DFPlayer Mini [part_number=DFR0299]
  SP1 = SPEAKER [package=pcb_mount_speaker]
  R8 = Resistor [tolerance=±5% resistance=1k package=THT]
  R9 = Rotary Potentiometer (Small) [maximum_resistance=100kΩ package=THT]
  Part3 = Arduino Mega ADK (Rev3)

nets:
  N1: Part1.A0, Part2.HORZ
  N2: Part1.A1, Part2.VERT
  N3: Part1.A2, R9.wiper
  N4: Part1.D13_PWM, DFRobot_DFPlayer_Mini1.TX
  N5: Part1.D12_PWM, R8.Pin_1
  N6: Part1.D11_PWM, S1.Pin_1, S1.Pin_2, R1.Pin_0
  N7: Part1.D10_PWM, S2.Pin_1, S2.Pin_2, R4.Pin_0
  N8: Part1.D9_PWM, S3.Pin_1, S3.Pin_2, R5.Pin_0
  N9: Part1.D8_PWM, S4.Pin_1, S4.Pin_2, R6.Pin_0
  5V: Part1.5V, S1.Pin_3, S1.Pin_4, S2.Pin_3, S2.Pin_4, S3.Pin_3, S3.Pin_4, S4.Pin_3, S4.Pin_4, Part2.VCC, DFRobot_DFPlayer_Mini1.VCC, R9.leg2, Part3.5V
  GND: Part1.GND, R1.Pin_1, R4.Pin_1, R6.Pin_1, Part2.GND, DFRobot_DFPlayer_Mini1.GND-1, DFRobot_DFPlayer_Mini1.GND-2, R9.leg1, Part3.GND
  N10: Part1.D0_RX0, Part3.D0/RX0
  N11: Part1.D1_TX0, Part3.D1/TX0
  N12: Part1.D2_PWM, Part3.D2_PWM
  N13: Part1.D3_PWM, Part3.D3_PWM
  N14: Part1.D4_PWM, Part3.D4_PWM
  N15: Part1.D5_PWM, Part3.D5_PWM
  N16: Part1.D6_PWM, Part3.D6_PWM
  N17: Part1.D7_PWM, Part3.D7_PWM
  N18: Part1.D22, Part3.D22
  N19: Part1.D23, Part3.D23
  N20: Part1.D24, Part3.D24
  N21: Part1.D25, Part3.D25
  N22: Part1.D26, Part3.D26
  N23: Part1.D27, Part3.D27
  N24: Part1.D28, Part3.D28
  N25: Part1.D29, Part3.D29
  N26: Part1.D30, Part3.D30
  N27: Part1.D31, Part3.D31
  N28: Part1.D32, Part3.D32
  N29: Part1.D33, Part3.D33
  N30: Part1.D34, Part3.D34
  N31: Part1.D35, Part3.D35
  N32: Part1.D36, Part3.D36
  N33: Part1.D37, Part3.D37
  N34: Part1.D38, Part3.D38
  N35: Part1.D39, Part3.D39
  N36: Part1.D40, Part3.D40
  N37: Part1.D41, Part3.D41
  N38: Part1.D42, Part3.D42
  N39: Part1.D43, Part3.D43
  N40: Part1.D44, Part3.D44
  N41: Part1.D45, Part3.D45
  N42: Part1.D46, Part3.D46
  N43: Part1.D47, Part3.D47
  N44: Part1.D48, Part3.D48
  N45: Part1.D49, Part3.D49
  N46: Part1.D50, Part3.D50/MISO
  N47: Part1.D51, Part3.D51/MOSI
  N48: Part1.D52, Part3.D52/SCK
  N49: Part1.D53, Part3.D53/SS
  N50: DFRobot_DFPlayer_Mini1.RX, R8.Pin_0
  N51: DFRobot_DFPlayer_Mini1.SPK_1, SP1.+
  N52: DFRobot_DFPlayer_Mini1.SPK_2, SP1.-
